// Logisim project Main bus.circ as structural Verilog: 1 circuit, main circuit Main bus
module Main_bus (
  input  in_1,
  input  in_2
);

  wire [6:0] keyboard_1_data;

  Counter #(.width(16), .max('hffff)) Program_counter ();  // open: load, D, count, Q, carry, clk, clr
  Register Memory_access_register ();  // open: D, en, Q, clk, clr
  Register Instruction_register ();  // open: D, en, Q, clk, clr
  RAM ram_1 ();  // open: addr, data, sel, clk, ld, clr
  ROM rom_1 ();  // open: addr, data, sel
  Keyboard keyboard_1 (.clk(in_1), .clr(in_2), .data(keyboard_1_data));  // open: re, avail
  TTY tty_1 (.data(keyboard_1_data), .clk(in_1), .clr(in_2));  // open: we
  Register Accumulator_register ();  // open: D, en, Q, clk, clr
  Register Input_register ();  // open: D, en, Q, clk, clr
  Register Output_register ();  // open: D, en, Q, clk, clr

  // Notes on the sheet:
  //   RAM for storage
  //   ROM for control matrix
  //   ALU
endmodule
